# Fritzing sketch AnalogReadSerial (saved by Fritzing 0.8.7b)
circuit board: 8.46667cm x 5.64444cm
breadboards: 1

parts:
  Biến_trở = Trimmer Potentiometer [maximum_resistance=10kΩ package=THT]
  Arduino_UNO_R3 = Arduino Uno (Rev3)

nets:
  N1: Biến_trở.leg1, Arduino_UNO_R3.GND
  N2: Biến_trở.wiper, Arduino_UNO_R3.A5/SCL
  N3: Biến_trở.leg2, Arduino_UNO_R3.5V

notes:
  Arduino.vn
