# Fritzing sketch DigitalReadSerial (saved by Fritzing 0.8.7b)
breadboards: 1

parts:
  Nút_nhấn = Momentary Switch [package=ksa_sealed_tac_switch]
  Điện_trở_10k_ohm = Resistor [tolerance=±5% resistance=10k package=THT]
  Arduino_UNO_R3 = Arduino Uno (Rev3)

nets:
  N1: Nút_nhấn.2, Điện_trở_10k_ohm.Pin_0
  N2: Nút_nhấn.3, Arduino_UNO_R3.D2
  N3: Nút_nhấn.4, Arduino_UNO_R3.5V
  N4: Điện_trở_10k_ohm.Pin_1, Arduino_UNO_R3.GND

notes:
  Arduino.vn
