# Fritzing sketch Zenner (saved by Fritzing 0.8.7b)
breadboards: 1

parts:
  R1 = Resistor [tolerance=±5% resistance=220 package=THT]
  Zenner = Zener Diode [part_number=1N4732A breakdown_voltage=3.6V package="300 mil [THT]"]
  5V = DC Power [voltage=5]
  Transistor = NPN-Transistor [package="TO92 [THT]"]
  Power_Out = Power plug

nets:
  N1: R1.Pin_0, 5V.V+, Transistor.C
  N2: R1.Pin_1, Zenner.cathode, Transistor.B
  N3: Zenner.anode, 5V.V-, Power_Out.GND
  N4: Transistor.E, Power_Out.VCC
